// Logisim project cpu.circ as structural Verilog: 5 circuits, main circuit contador-8bits
// CPU
module main (
  input  clock,
  input  preset,
  input  unidade_de_controle_a_fazer,
  input  clear,
  output [15:0] \saída_da_memória ,
  output [7:0] debug_do_contador
);

  wire ULA_p2;

  contador_8bits Contador___8_bits (.clock(clock), .clear(preset), .preset(clear), .out_4(debug_do_contador));
  registrador_4bits Registrador_1 ();  // open: clock, preset, clear, q0, q1, q2, q3, d0, d1, d2, d3
  ROM #(.dataWidth(16), .Select("low")) ROM (.addr(debug_do_contador), .data(\saída_da_memória ));
  // ULA_main ULA: pin names not known; wires that end beside it: unidade_de_controle_a_fazer, ULA_p2, ULA_p2
  registrador_4bits Registrador_2 ();  // open: clock, preset, clear, q0, q1, q2, q3, d0, d1, d2, d3

  // Notes on the sheet:
  //   contents of ROM (hex, n*v repeats v):
  //   3000 239*0 23
endmodule

module contador_8bits (
  input  clock,
  input  clear,
  input  preset,
  output [7:0] out_4
);

  wire and_1_out, and_2_out, and_3_out, and_4_out, and_5_out, and_6_out;

  J_K_Flip_Flop j_k_ff_1 (.J(1'b1), .clk(clock), .K(1'b1), .Q(out_4[0]), .preset(preset), .reset(clear));  // open: Qn
  J_K_Flip_Flop j_k_ff_2 (
    .J(out_4[0]), .clk(clock), .K(out_4[0]), .Q(out_4[1]), .preset(preset), .reset(clear));  // open: Qn
  and and_1 (and_1_out, out_4[0], out_4[1]);
  J_K_Flip_Flop j_k_ff_3 (
    .J(and_1_out), .clk(clock), .K(and_1_out), .Q(out_4[2]), .preset(preset), .reset(clear));  // open: Qn
  and and_2 (and_2_out, and_1_out, out_4[2]);
  J_K_Flip_Flop j_k_ff_4 (
    .J(and_2_out), .clk(clock), .K(and_2_out), .Q(out_4[3]), .preset(preset), .reset(clear));  // open: Qn
  and and_3 (and_3_out, and_2_out, out_4[3]);
  J_K_Flip_Flop j_k_ff_5 (
    .J(and_3_out), .clk(clock), .K(and_3_out), .Q(out_4[4]), .preset(preset), .reset(clear));  // open: Qn
  and and_4 (and_4_out, and_3_out, out_4[4]);
  J_K_Flip_Flop j_k_ff_6 (
    .J(and_4_out), .clk(clock), .K(and_4_out), .Q(out_4[5]), .preset(preset), .reset(clear));  // open: Qn
  and and_5 (and_5_out, and_4_out, out_4[5]);
  J_K_Flip_Flop j_k_ff_7 (
    .J(and_5_out), .clk(clock), .K(and_5_out), .Q(out_4[6]), .preset(preset), .reset(clear));  // open: Qn
  and and_6 (and_6_out, and_5_out, out_4[6]);
  J_K_Flip_Flop j_k_ff_8 (
    .J(and_6_out), .clk(clock), .K(and_6_out), .Q(out_4[7]), .preset(preset), .reset(clear));  // open: Qn
endmodule

module registrador_4bits (
  input  clock,
  input  preset,
  input  clear,
  input  d0,
  input  d1,
  input  d2,
  input  d3,
  output q0,
  output q1,
  output q2,
  output q3
);

  wire d_ff_2_qn;

  D_Flip_Flop #(.Pre_Clr_Positions("LEGACY")) d_ff_1 (
    .clk(clock), .D(d0), .Q(q0), .preset(preset), .reset(clear));  // open: Qn
  D_Flip_Flop d_ff_2 (.clk(clock), .D(d1), .Q(q1), .Qn(d_ff_2_qn), .preset(preset), .reset(clear));
  D_Flip_Flop d_ff_3 (.clk(clock), .D(d2), .Q(q2), .preset(preset), .reset(clear));  // open: Qn
  D_Flip_Flop d_ff_4 (.clk(clock), .D(d3), .Q(q3), .reset(clear));  // open: Qn, preset
endmodule

module ULA (
  input  [3:0] in_1,
  input  [3:0] in_2,
  input  [1:0] in_3,
  output [3:0] out_4,
  output [3:0] out_5,
  output [3:0] out_6,
  output [3:0] out_7,
  output [3:0] out_8
);

  Adder #(.width(4)) adder_1 (.a(in_1), .b(in_2), .out(out_4));  // open: cin, cout
  Multiplier #(.width(4)) multiplier_1 (.a(in_1), .b(4'b0010), .out(out_5));  // open: cin, cout
  Subtractor #(.width(4)) subtractor_1 (.a(in_1), .b(in_2), .out(out_6));  // open: bin, bout
  Divider #(.width(4)) divider_1 (.a(in_1), .b(4'b0010), .out(out_8));  // open: upper, rem
  Multiplexer #(.select(2), .width(4), .enable("false")) multiplexer_1 (
    .in0(out_4), .in1(out_5), .in2(out_6), .in3(out_8), .out(out_7), .sel(in_3));
endmodule

module DE0cv (
  input  clear
);

  wire K0, K1, K2, K3, L0, L1, L2, L3, L4, L5, L6, L7, L8, L9, S0, S1, S2, S3, S4, S5, S6, S7, S8, S9;
  wire [3:0] HEX0, HEX1, HEX2, HEX3, HEX4, HEX5;

  Hex_Digit_Display hex_digit_display_1 (.value(HEX5));  // open: dp
  LED u_L9 (.in(L9));
  LED u_L8 (.in(L8));
  // DipSwitch #(.NSwitches(1)) S9: pin names not known; wires that end beside it: S9
  // DipSwitch #(.NSwitches(1)) S8: pin names not known; wires that end beside it: S8
  Hex_Digit_Display hex_digit_display_2 (.value(HEX3));  // open: dp
  Hex_Digit_Display hex_digit_display_3 (.value(HEX4));  // open: dp
  LED u_L7 (.in(L7));
  LED u_L6 (.in(L6));
  LED u_L5 (.in(L5));
  // DipSwitch #(.NSwitches(1)) S5: pin names not known; wires that end beside it: S5
  // DipSwitch #(.NSwitches(1)) S7: pin names not known; wires that end beside it: S7
  // DipSwitch #(.NSwitches(1)) S6: pin names not known; wires that end beside it: S6
  Hex_Digit_Display hex_digit_display_4 (.value(HEX2));  // open: dp
  LED u_L3 (.in(L3));
  LED u_L4 (.in(L4));
  // DipSwitch #(.NSwitches(1)) S4: pin names not known; wires that end beside it: S4
  // DipSwitch #(.NSwitches(1)) S2: pin names not known; wires that end beside it: S2
  // DipSwitch #(.NSwitches(1)) S3: pin names not known; wires that end beside it: S3
  Hex_Digit_Display hex_digit_display_5 (.value(HEX1));  // open: dp
  Hex_Digit_Display hex_digit_display_6 (.value(HEX0));  // open: dp
  LED u_L0 (.in(L0));
  LED u_L1 (.in(L1));
  LED u_L2 (.in(L2));
  // DipSwitch #(.NSwitches(1)) S1: pin names not known; wires that end beside it: S1
  // DipSwitch #(.NSwitches(1)) S0: pin names not known; wires that end beside it: S0
  Button u_K2 (.out(K2));
  Button u_K3 (.out(K3));
  Button u_K1 (.out(K1));
  Button u_K0 (.out(K0));
  // Digital_Oscilloscope #(.nState(22)) digital_oscilloscope_1: pin names not known; wires that end beside it: S9, L0, L2, L3, L4, L5, L6, L7, L1, 1'b1, clear
  contador_8bits Contador___8_bits (.clock(S9), .clear(S0), .out_4({L7, L6, L5, L4, L3, L2, L1, L0}));  // open: preset
  ROM #(.dataWidth(16), .Select("low")) ROM (.addr({L7, L6, L5, L4, L3, L2, L1, L0}), .data({HEX5, HEX4, HEX3, HEX2}));
  // ULA_main ULA: pin names not known
  registrador_4bits Registrador_2 ();  // open: clock, preset, clear, q0, q1, q2, q3, d0, d1, d2, d3
  registrador_4bits Registrador_1 ();  // open: clock, preset, clear, q0, q1, q2, q3, d0, d1, d2, d3

  // Notes on the sheet:
  //   Clock S9 - Clear S0 - Memória HEX5-HEX2 - Contador L0-L7
  //   contents of ROM (hex, n*v repeats v):
  //   6005 9101 6202 6304 c08 0 0 0 400 6001 9001 9002 6302 6102 9302 6200 6001 800
endmodule
